# Fritzing sketch led-18 (saved by Fritzing 0.7.12b)
breadboards: 1

parts:
  Raspberry_Pi1 = Raspberry Pi (Model B)
  R1 = Resistor [tolerance=±5% resistance=330 package=THT]
  LED1 = LED - 5mm [color="Red (633nm)" package="5 mm [THT]"]

nets:
  N1: Raspberry_Pi1.GND, R1.Pin_0
  N2: Raspberry_Pi1.#18, LED1.anode
  N3: R1.Pin_1, LED1.cathode

custom parts:
  Raspberry Pi (Model B): Raspberry Pi Single-board Computer, Model B
