# Fritzing sketch rangefinder (saved by Fritzing 0.7.12b)
breadboards: 1

parts:
  Raspberry_Pi1 = Raspberry Pi (Model B)
  Part1 = SRF05 Ultrasonic Rangefinder
  R2 = Resistor [tolerance=±5% resistance=330 package=THT]
  R3 = Resistor [tolerance=±5% resistance=470 package=THT]

nets:
  N1: Raspberry_Pi1.5V, Part1.5v_Supply
  N2: Raspberry_Pi1.GND, Part1.Ground, R3.Pin_0
  N3: Raspberry_Pi1.#23, R2.Pin_0, R3.Pin_1
  N4: Raspberry_Pi1.#24, Part1.Echo_Output, Part1.Trigger_Input, Part1.Mode_(not_used), R2.Pin_1

notes:
  360 ohm resistor
  470 ohm resistor

custom parts:
  Raspberry Pi (Model B): Raspberry Pi Single-board Computer, Model B
